// Logisim project MpMp25.circ as structural Verilog: 6 circuits, main circuit main
module main (
  input  RST
);

  wire ALU_AccuEn, ALU_CE, ALU_F_E, and_1_out, and_2_out, and_3_out, CLK, cu_1_clk_qtr, cu_1_io_input,
       cu_1_lng_jmp, cu_1_rf_ce0, cu_1_rf_ce1, cu_1_rf_data_out_0_e, cu_1_rf_pt_e, cu_1_rf_w_nr,
       decoder_1_out0, decoder_1_out1, decoder_1_out2, decoder_1_out3, decoder_1_out4, decoder_1_out5,
       decoder_2_out0, decoder_2_out1, decoder_2_out2, decoder_2_out3, decoder_2_out4, decoder_2_out5,
       decoder_2_out6, decoder_3_out0, decoder_3_out1, or_1_out, RAM_CE, RAM_WE;
  wire [0:0] keyboard_1_avail;
  wire [2:0] cu_1_reg0, cu_1_reg1;
  wire [3:0] ALU_CMD, joystick_1_x, joystick_1_y, rf_1_pc;
  wire [6:0] keyboard_1_data;
  wire [7:0] Addr, alu_1_flag_out, alu_1_result, ALU_F_IN, IO_8_B_q, IO_9_G_q, IO_a_R_q, IO_D_X_q, IO_F_Y_q,
       MEMORY, ram_1_dout, register_1_q, register_2_q, rf_1_data_out0;
  wire [7:4] rf_1_pc_2;
  wire [15:0] rom_1_data;

  Clock clock_1 (.out(CLK));
  CU cu_1 (
    .CLK(CLK), .RST(RST), .Instruction(rom_1_data), .ALU_F_IN(ALU_F_IN), .Reg0(cu_1_reg0), .Reg1(cu_1_reg1),
    .\const (MEMORY), .RF_W_nR(cu_1_rf_w_nr), .RF_CE0(cu_1_rf_ce0), .RF_CE1(cu_1_rf_ce1),
    .ALU_AccuEn(ALU_AccuEn), .ALU_CE(ALU_CE), .RAM_WE(RAM_WE), .RAM_CE(RAM_CE), .ALU_CMD(ALU_CMD),
    .RF_PT_E(cu_1_rf_pt_e), .CLK_QTR(cu_1_clk_qtr), .RF_Data_Out_0_E(cu_1_rf_data_out_0_e),
    .IO_Input(cu_1_io_input), .ADDR(Addr), .ALU_F_E(ALU_F_E), .LNG_JMP(cu_1_lng_jmp));  // open: RegResult
  assign MEMORY = cu_1_lng_jmp ? {{5{1'b0}}, cu_1_reg0} : 8'bz;  // Controlled_Buffer controlled_buffer_1
  Hex_Digit_Display #(.decimalPoint("false")) hex_digit_display_1 (.value(MEMORY[7:4]));
  Hex_Digit_Display #(.decimalPoint("false")) hex_digit_display_2 (.value(MEMORY[3:0]));
  Hex_Digit_Display #(.decimalPoint("false")) hex_digit_display_3 (.value(rf_1_pc));
  Hex_Digit_Display #(.decimalPoint("false")) hex_digit_display_4 (.value(rf_1_pc_2));
  RF rf_1 (
    .Addr0(cu_1_reg0), .Addr1(cu_1_reg1), .Data_In(MEMORY), .W_nR(cu_1_rf_w_nr), .CE0(cu_1_rf_ce0),
    .CE1(cu_1_rf_ce1), .CLK(CLK), .RST(RST), .PTR_E(cu_1_rf_pt_e), .CLK_QTR(cu_1_clk_qtr),
    .Data_OUT0(rf_1_data_out0), .Data_OUT1(MEMORY), .PC({rf_1_pc_2, rf_1_pc}), .PointerReg(Addr));
  ROM #(.addrWidth(16), .dataWidth(16)) rom_1 (.addr({MEMORY, rf_1_pc_2, rf_1_pc}), .data(rom_1_data));
  ALU alu_1 (
    .Flag_In(ALU_F_IN), .CMD_15_12(ALU_CMD), .Op0(rf_1_data_out0), .Op1(MEMORY), .Result(alu_1_result),
    .Flag_Out(alu_1_flag_out));
  Decoder #(.select(3)) decoder_1 (
    .out0(decoder_1_out0), .out1(decoder_1_out1), .out2(decoder_1_out2), .out3(decoder_1_out3),
    .out4(decoder_1_out4), .out5(decoder_1_out5), .sel(Addr[2:0]), .en(and_1_out));  // open: out6, out7
  and and_1 (and_1_out, ~Addr[3], ~Addr[4], ~Addr[5], ~Addr[6], ~Addr[7], cu_1_io_input);  // AND_Gate
  and and_2 (and_2_out, Addr[3], ~Addr[4], ~Addr[5], ~Addr[6], ~Addr[7], cu_1_io_input);  // AND_Gate
  and and_3 (and_3_out, Addr[3], ~Addr[4], ~Addr[5], ~Addr[6], ~Addr[7], cu_1_io_input);  // AND_Gate
  assign MEMORY = ALU_CE ? register_1_q : 8'bz;  // Controlled_Buffer controlled_buffer_2
  Register register_1 (.D(alu_1_result), .en(ALU_AccuEn), .Q(register_1_q), .clk(CLK), .clr(RST));
  Decoder #(.select(3)) decoder_2 (
    .out0(decoder_2_out0), .out1(decoder_2_out1), .out2(decoder_2_out2), .out3(decoder_2_out3),
    .out4(decoder_2_out4), .out5(decoder_2_out5), .out6(decoder_2_out6), .sel(Addr[2:0]), .en(and_2_out));  // open: out7
  Decoder #(.select(3)) decoder_3 (
    .out0(decoder_3_out0), .out1(decoder_3_out1), .sel(Addr[2:0]), .en(and_3_out));  // open: out2, out3, out4, out5, out6, out7
  assign MEMORY = cu_1_rf_data_out_0_e ? rf_1_data_out0 : 8'bz;  // Controlled_Buffer controlled_buffer_3
  Register register_2 (.D(MEMORY), .en(decoder_3_out1), .clk(CLK), .Q(register_2_q), .clr(RST));
  RAM ram_1 (.addr(Addr), .we(RAM_WE), .oe(RAM_CE), .clk(CLK), .din(MEMORY), .dout(ram_1_dout));
  TTY tty_1 (.data(MEMORY[6:0]), .clk(CLK), .we(decoder_1_out0), .clr(decoder_1_out1));
  Keyboard keyboard_1 (
    .clk(CLK), .re(decoder_1_out2), .clr(decoder_1_out4), .avail(keyboard_1_avail[0]), .data(keyboard_1_data));
  Register IO_8_B (.D(MEMORY), .en(decoder_2_out0), .Q(IO_8_B_q), .clk(CLK), .clr(RST));
  Register IO_9_G (.D(MEMORY), .en(decoder_2_out1), .Q(IO_9_G_q), .clk(CLK), .clr(RST));
  Register IO_a_R (.D(MEMORY), .en(decoder_2_out2), .Q(IO_a_R_q), .clk(CLK), .clr(RST));
  Register IO_D_X (.D(MEMORY), .en(decoder_2_out5), .Q(IO_D_X_q), .clk(CLK), .clr(RST));
  Register IO_F_Y (.D(MEMORY), .en(decoder_2_out6), .Q(IO_F_Y_q), .clk(CLK), .clr(RST));
  Register register_3 (.D(alu_1_flag_out), .en(ALU_F_E), .Q(ALU_F_IN), .clk(CLK), .clr(RST));
  assign MEMORY = decoder_3_out0 ? register_2_q : 8'bz;  // Controlled_Buffer controlled_buffer_4
  or or_1 (or_1_out, RST, decoder_2_out3);
  assign MEMORY = RAM_CE ? ram_1_dout : 8'bz;  // Controlled_Buffer controlled_buffer_5
  assign MEMORY = decoder_1_out2 ? {1'b0, keyboard_1_data} : 8'bz;  // Controlled_Buffer controlled_buffer_6
  assign MEMORY = decoder_1_out3 ? {{7{1'b0}}, keyboard_1_avail[0]} : 8'bz;  // Controlled_Buffer controlled_buffer_7
  // RGB_Video #(.height(256), .width(256)) rgb_video_1: pin names not known; wires that end beside it: or_1_out, CLK, decoder_2_out4, IO_D_X_q, IO_F_Y_q, {IO_a_R_q, IO_9_G_q, IO_8_B_q}
  Joystick joystick_1 (.x(joystick_1_x), .y(joystick_1_y));
  assign MEMORY = decoder_1_out5 ? {joystick_1_y, joystick_1_x} : 8'bz;  // Controlled_Buffer controlled_buffer_8

  // Notes on the sheet:
  //   Instruction bus
  //   guck bei Ludger
  //   Data bus
  //   guck bei Ludger
  //   contents of rom_1 (hex, n*v repeats v):
  //   1151 9812
  //   CE
  //   in Hexanzeige von Program Memory dann 0100, wenn auf nächster Seite
  //   Paging Register
  //   256 Worte x 256 Seiten
  //   Pages: 0...FF, 100...1FF, ...
  //   damit 65 kB RAM
  //   blank
  //   strope
  //   guck bei Ludger
endmodule

module ALU (
  input  [7:0] Op0,
  input  [7:0] Op1,
  input  [3:0] CMD_15_12,
  input  [7:0] Flag_In,
  output [7:0] Result,
  output [7:0] Flag_Out
);

  wire ADD_OFlag_Res, adder_1_cout, adder_2_cout, and_2_out, and_3_out, and_4_out, and_5_out,
       comparator_2_eq, multiplexer_1_out, multiplexer_3_out, multiplexer_4_out, R, shiftl_1_cout,
       SUB_OFlag_Res, subtractor_1_bout, subtractor_2_bout, xor_2_out, Z_out;
  wire [0:0] undriven;
  wire [3:0] undriven_2;
  wire [7:0] adder_1_out, adder_2_out, and_1_out, divider_1_out, divider_1_rem, Flag_Select_data,
       multiplier_1_out, negator_1_out, not_1_out, or_1_out, shiftl_1_result, subtractor_1_out,
       subtractor_2_out, undriven_3, xnor_1_out, xor_1_out;
  wire [8:0] shifter_2_out, shifter_3_out;
  wire [9:0] shifter_1_out;

  // Probe on Op0
  // Probe on Op0
  // Probe on Op1
  // Probe on Op1
  Adder adder_1 (.a(Op0), .b(Op1), .out(adder_1_out), .cout(adder_1_cout));  // open: cin
  Subtractor subtractor_1 (.a(Op1), .b(Op0), .out(subtractor_1_out), .bout(subtractor_1_bout));  // open: bin
  Multiplier multiplier_1 (.a(Op0), .b(Op1), .out(multiplier_1_out));  // open: cin, cout
  Divider divider_1 (.a(Op1), .b(Op0), .out(divider_1_out), .upper({8{1'b0}}), .rem(divider_1_rem));
  Negator negator_1 (.in(Op1), .out(negator_1_out));
  assign and_1_out = Op1 & Op0;  // AND_Gate and_1, 8 bits wide
  assign or_1_out = Op1 | Op0;  // OR_Gate or_1, 8 bits wide
  assign xor_1_out = Op1 ^ Op0;  // XOR_Gate xor_1, 8 bits wide
  assign xnor_1_out = ~(Op0 ^ Op1);  // XNOR_Gate xnor_1, 8 bits wide
  assign not_1_out = ~Op1;  // NOT_Gate not_1, 8 bits wide
  Adder adder_2 (.a(Op1), .b(Op0), .out(adder_2_out), .cin(Flag_In[1]), .cout(adder_2_cout));
  Subtractor subtractor_2 (.a(Op1), .b(Op0), .out(subtractor_2_out), .bin(Flag_In[1]), .bout(subtractor_2_bout));
  ROM #(.addrWidth(4)) Flag_Select (.addr(CMD_15_12), .data(Flag_Select_data));
  Comparator comparator_1 (.a({8{1'b0}}), .b(divider_1_rem), .gt(R));  // open: eq, lt
  ShiftL shiftl_1 (.Op(Op1), .Dist(Op0), .CIn(Flag_In[1]), .Result(shiftl_1_result), .COut(shiftl_1_cout));
  Shifter #(.shift("lr"), .width(10)) shifter_1 (
    .in({Flag_In[1], Op1, undriven[0]}), .\dist (Op0[3:0]), .out(shifter_1_out));
  Comparator comparator_2 (.a(Op0), .b({8{1'b0}}), .eq(comparator_2_eq));  // open: gt, lt
  Multiplexer #(.select(4)) multiplexer_1 (
    .in0(Flag_In[3]), .in1(Flag_In[3]), .in2(Flag_In[3]), .in3(comparator_2_eq), .in4(Flag_In[3]),
    .in5(Flag_In[3]), .in6(Flag_In[3]), .in7(Flag_In[3]), .in8(Flag_In[3]), .in9(Flag_In[3]),
    .in10(Flag_In[3]), .in11(Flag_In[3]), .in12(Flag_In[3]), .in13(Flag_In[3]), .in14(Flag_In[3]),
    .in15(Flag_In[3]), .out(multiplexer_1_out), .sel(CMD_15_12));
  xor xor_2 (xor_2_out, Result[7], Op1[7]);
  Multiplexer #(.select(4), .width(8)) multiplexer_2 (
    .in0(adder_1_out), .in1(subtractor_1_out), .in2(multiplier_1_out), .in3(divider_1_out),
    .in4(shiftl_1_result), .in5(shifter_1_out[8:1]), .in6(negator_1_out), .in7({8{1'b0}}), .in8({8{1'b0}}),
    .in9(and_1_out), .in10(or_1_out), .in11(xor_1_out), .in12(xnor_1_out), .in13(not_1_out),
    .in14(adder_2_out), .in15(subtractor_2_out), .out(Result), .sel(CMD_15_12));
  Multiplexer #(.select(4)) multiplexer_3 (
    .in0(adder_1_cout), .in1(subtractor_1_bout), .in2(Flag_In[1]), .in3(Flag_In[1]), .in4(shiftl_1_cout),
    .in5(shifter_1_out[9]), .in6(Flag_In[1]), .in7(Flag_In[1]), .in8(Flag_In[1]), .in9(Flag_In[1]),
    .in10(Flag_In[1]), .in11(Flag_In[1]), .in12(Flag_In[1]), .in13(Flag_In[1]), .in14(adder_2_cout),
    .in15(subtractor_2_bout), .out(multiplexer_3_out), .sel(CMD_15_12));
  Multiplexer #(.select(4)) multiplexer_4 (
    .in0(xor_2_out), .in1(xor_2_out), .in2(xor_2_out), .in3(Flag_In[2]), .in4(Flag_In[2]), .in5(Flag_In[2]),
    .in6(Flag_In[2]), .in7(Flag_In[2]), .in8(Flag_In[2]), .in9(Flag_In[2]), .in10(Flag_In[2]),
    .in11(Flag_In[2]), .in12(Flag_In[2]), .in13(Flag_In[2]), .in14(xor_2_out), .in15(xor_2_out),
    .out(multiplexer_4_out), .sel(CMD_15_12));
  // Probe on Result
  Multiplexer multiplexer_5 (.in0(Flag_In[0]), .in1(Z_out), .out(Flag_Out[0]), .sel(Flag_Select_data[0]));
  Multiplexer multiplexer_6 (.in0(Flag_In[1]), .in1(multiplexer_3_out), .out(Flag_Out[1]), .sel(Flag_Select_data[1]));
  Multiplexer multiplexer_7 (.in0(Flag_In[2]), .in1(multiplexer_4_out), .out(Flag_Out[2]), .sel(Flag_Select_data[2]));
  Multiplexer multiplexer_8 (.in0(Flag_In[3]), .in1(multiplexer_1_out), .out(Flag_Out[3]), .sel(Flag_Select_data[3]));
  Multiplexer multiplexer_9 (.in0(Flag_In[4]), .in1(R), .out(Flag_Out[4]), .sel(Flag_Select_data[4]));
  nor Z (Z_out, Result[0], Result[1], Result[2], Result[3], Result[4], Result[5], Result[6], Result[7]);
  // Probe on Op0
  // Probe on Op1
  // Probe on Result
  and and_2 (and_2_out, ~Op0[7], ~Op1[7], Result[7]);  // AND_Gate
  and and_3 (and_3_out, Op0[7], Op1[7], ~Result[7]);  // AND_Gate
  and and_4 (and_4_out, Op0[7], ~Op1[7], ~Result[7]);  // AND_Gate
  and and_5 (and_5_out, ~Op0[7], Op1[7], Result[7]);  // AND_Gate
  or or_2 (ADD_OFlag_Res, and_2_out, and_3_out);
  or or_3 (SUB_OFlag_Res, and_4_out, and_5_out);
  Shifter #(.width(9)) shifter_2 (.in({undriven_3, Flag_In[1]}), .\dist (undriven_2), .out(shifter_2_out));
  Shifter #(.shift("lr"), .width(9)) shifter_3 (.in({Flag_In[1], undriven_3}), .out(shifter_3_out));  // open: dist

  assign Flag_Out[7:5] = Flag_In[7:5];

  // Other names for the same wires on the sheet: Op1_Tunnel[7:0] = Op1; C = Flag_In[1]; Op0_Tunnel[7:0] = Op0

  // Notes on the sheet:
  //   ADD 0, SUB 1, ADDC 14; SUBC 15
  //   ADD 0x00, SUB 0x01, ADDC 0x0E; SUBC 0x0F
  //   +-
  //   +-
  //   Op0
  //   Op1
  //   Op1 kommt immer zuerst; guck in Git!
  //   contents of Flag_Select (hex, n*v repeats v):
  //   7 7 7 39 10*1 7 7
  //     XXX,overflow_O, carry_C, zero_Z
  //   C_Flag
  //   O_Flag
  //   Z_Flag
  //   C_Flag
  //   O_Flag
  //   E_Flag
  //   R_Flag
  //   O_Flag ADD
  //   O_Flag SUB
  //   --> vielleicht mit xor
  //   Shift mit Carry
  //   C_Flag Mux
  //   Result Mux
endmodule

module CU (
  input  CLK,
  input  RST,
  input  [15:0] Instruction,
  input  [7:0] ALU_F_IN,
  output [2:0] Reg0,
  output [2:0] Reg1,
  output [2:0] RegResult,
  output [7:0] \const ,
  output RF_W_nR,
  output RF_CE0,
  output RF_CE1,
  output ALU_AccuEn,
  output ALU_CE,
  output RAM_WE,
  output RAM_CE,
  output [3:0] ALU_CMD,
  output RF_PT_E,
  output CLK_QTR,
  output RF_Data_Out_0_E,
  output IO_Input,
  output [7:0] ADDR,
  output ALU_F_E,
  output LNG_JMP
);

  wire Cycle_Zero, multiplexer_1_out;
  wire [1:0] Cyclecounter_q, rom_1_data_3;
  wire [2:0] Reg0_t, Reg1_t, register_1_q, RegResult_t;
  wire [3:0] rom_1_data_2;
  wire [3:3] register_1_q_2;
  wire [6:4] and_2_out;
  wire [7:0] multiplexer_2_out;
  wire [9:9] xor_1_out;
  wire [11:6] IR_q;
  wire [31:7] rom_1_data;

  Register #(.trigger("falling"), .width(16)) IR (
    .D(Instruction), .clk(Cycle_Zero), .Q({ALU_CMD, IR_q[11], RegResult_t, IR_q[7:6], Reg1_t, Reg0_t}),
    .clr(RST));  // open: en
  Counter #(.max('h3), .width(2)) Cyclecounter (
    .Q(Cyclecounter_q), .carry(CLK_QTR), .clk(CLK), .clr(RST));  // open: load, D, count, up
  Multiplexer #(.select(3)) multiplexer_1 (
    .in0(1'b0), .in1(ALU_F_IN[0]), .in2(ALU_F_IN[1]), .in3(ALU_F_IN[2]), .in4(ALU_F_IN[3]),
    .in5(ALU_F_IN[4]), .in6(ALU_F_IN[5]), .in7(ALU_F_IN[6]), .out(multiplexer_1_out), .sel(register_1_q));
  and and_1 (and_2_out[6], IR_q[7], ~IR_q[11]);  // AND_Gate
  and and_2 (and_2_out[4], ~IR_q[11], IR_q[6]);  // AND_Gate
  nor nor_1 (Cycle_Zero, Cyclecounter_q[0], Cyclecounter_q[1]);
  Multiplexer #(.width(8)) multiplexer_2 (
    .in0({{5{1'b0}}, Reg0_t}), .in1({IR_q[7:6], Reg1_t, Reg0_t}), .out(multiplexer_2_out), .sel(IR_q[11]));
  xor xor_1 (xor_1_out[9], multiplexer_1_out, register_1_q_2[3]);
  ROM #(.addrWidth(10), .dataWidth(32)) rom_1 (
    .addr({xor_1_out[9], and_2_out[6], IR_q[11], and_2_out[4], ALU_CMD, Cyclecounter_q}),
    .data({rom_1_data[31:20], LNG_JMP, rom_1_data_2, ALU_F_E, rom_1_data[13], IO_Input, RF_Data_Out_0_E, rom_1_data_3[1], RF_PT_E, rom_1_data_3[0], rom_1_data[7], RAM_CE, RAM_WE, ALU_CE, ALU_AccuEn, RF_CE1, RF_CE0, RF_W_nR}));
  assign \const  = rom_1_data[7] ? multiplexer_2_out : 8'bz;  // Controlled_Buffer controlled_buffer_1
  Multiplexer #(.select(2), .width(3)) multiplexer_3 (
    .in0(RegResult_t), .in1(Reg0_t), .in2(Reg1_t), .out(Reg0), .sel(rom_1_data_3));  // open: in3
  assign ADDR = rom_1_data[13] ? multiplexer_2_out : 8'bz;  // Controlled_Buffer controlled_buffer_2
  Register #(.width(4)) register_1 (
    .D(rom_1_data_2), .Q({register_1_q_2[3], register_1_q}), .clk(CLK), .clr(RST));  // open: en
  Multiplexer #(.width(3)) multiplexer_4 (.in0(Reg1_t), .in1(RegResult_t), .out(Reg1), .sel(rom_1_data_3[1]));

  // Notes on the sheet:
  //   IR
  //   Instruction Register
  //   IMOPb[7]
  //   IMOPa[11]
  //   CMD[6]
  //   CMD_const_8
  //   CMD0[15...12]
  //   2-0 Op0
  //   5-3 Op1
  //   10-8 RegR
  //   contents of rom_1 (hex, n*v repeats v):
  //   0 4 5 0 0 0 4 4 9*0 241 241 14*0 200 a02 130*0 8000 81 81 13*0 3404 0 0 0 3001 3001 2 80 1 63*0 81 1
  //   80 235*0 8
  //   const_en
  //   Reg_ResOn0
  //   Reg_SLC
  //   Flag_Select_0
  //   Flag_Select_1
  //   Flag_Select_2
  //   Flag_neg
  //   Addr_E
  //   UV
endmodule

module RF (
  input  [2:0] Addr0,
  input  [2:0] Addr1,
  input  [7:0] Data_In,
  input  W_nR,
  input  CE0,
  input  CE1,
  input  CLK,
  input  RST,
  input  PTR_E,
  input  CLK_QTR,
  output [7:0] Data_OUT0,
  output [7:0] Data_OUT1,
  output [7:0] PC,
  output [7:0] PointerReg
);

  wire decoder_1_out0, decoder_1_out1, decoder_1_out2, decoder_1_out3, decoder_1_out4, decoder_1_out5,
       decoder_1_out6, decoder_1_out7;
  wire [7:0] register_1_q, register_2_q, register_3_q, register_4_q, register_5_q, register_6_q, register_7_q;

  Decoder #(.select(3)) decoder_1 (
    .out0(decoder_1_out0), .out1(decoder_1_out1), .out2(decoder_1_out2), .out3(decoder_1_out3),
    .out4(decoder_1_out4), .out5(decoder_1_out5), .out6(decoder_1_out6), .out7(decoder_1_out7), .sel(Addr0),
    .en(W_nR));
  Counter counter_1 (
    .load(decoder_1_out0), .D(Data_In), .count(CLK_QTR), .Q(PC), .clk(CLK), .clr(RST));  // open: carry, up
  Register register_1 (.D(Data_In), .en(decoder_1_out1), .Q(register_1_q), .clk(CLK), .clr(RST));
  Register register_2 (.D(Data_In), .en(decoder_1_out2), .Q(register_2_q), .clk(CLK), .clr(RST));
  Register register_3 (.D(Data_In), .en(decoder_1_out3), .Q(register_3_q), .clk(CLK), .clr(RST));
  Register register_4 (.D(Data_In), .en(decoder_1_out4), .Q(register_4_q), .clk(CLK), .clr(RST));
  Register register_5 (.D(Data_In), .en(decoder_1_out5), .Q(register_5_q), .clk(CLK), .clr(RST));
  Register register_6 (.D(Data_In), .en(decoder_1_out6), .Q(register_6_q), .clk(CLK), .clr(RST));
  Register register_7 (.D(Data_In), .en(decoder_1_out7), .Q(register_7_q), .clk(CLK), .clr(RST));
  Multiplexer #(.disabled("Z"), .enable("true"), .select(3), .width(8)) multiplexer_1 (
    .in0(PC), .in1(register_1_q), .in2(register_2_q), .in3(register_3_q), .in4(register_4_q),
    .in5(register_5_q), .in6(register_6_q), .in7(register_7_q), .out(Data_OUT0), .sel(Addr0), .en(CE0));
  Multiplexer #(.disabled("Z"), .enable("true"), .select(3), .width(8)) multiplexer_2 (
    .in0(PC), .in1(register_1_q), .in2(register_2_q), .in3(register_3_q), .in4(register_4_q),
    .in5(register_5_q), .in6(register_6_q), .in7(register_7_q), .out(Data_OUT1), .sel(Addr1), .en(CE1));
  Multiplexer #(.disabled("Z"), .enable("true"), .select(3), .width(8)) multiplexer_3 (
    .in0(PC), .in1(register_1_q), .in2(register_2_q), .in3(register_3_q), .in4(register_4_q),
    .in5(register_5_q), .in6(register_6_q), .in7(register_7_q), .out(PointerReg), .sel(Addr1), .en(PTR_E));

  // Notes on the sheet:
  //   Registerfile
  //   speicher in dem register sind 
  //   Speicherdecoder wann geschrieben wird
  //   Read notWrite
  //   Chipenable
  //   1
  //   6
  //   Pc
  //   2
  //   3
  //   4
  //   5
  //   7
endmodule

module test_ALU (
);

  wire and_1_out, and_2_out, clock_1_out, comparator_1_eq, comparator_2_eq;
  wire [3:0] ALU_Command_data;
  wire [7:0] alu_1_flag_out, alu_1_result, Flag_result_data, Flags_In_data, Op0_data, Op1_data, Result_data;
  wire [9:0] Adresse;

  Clock clock_1 (.out(clock_1_out));
  Hex_Digit_Display hex_digit_display_1 (.value({2'b00, Adresse[9:8]}));  // open: dp
  Hex_Digit_Display hex_digit_display_2 (.value(Adresse[7:4]));  // open: dp
  and and_1 (and_1_out, clock_1_out, and_2_out);
  Hex_Digit_Display hex_digit_display_3 (.value(Adresse[3:0]));  // open: dp
  Counter #(.max('h3ff), .trigger("falling"), .width(10)) counter_1 (
    .Q(Adresse), .clk(and_1_out));  // open: load, D, count, carry, up, clr
  ROM #(.addrWidth(10), .dataWidth(4)) ALU_Command (.addr(Adresse), .data(ALU_Command_data));
  ROM #(.addrWidth(10)) Op0 (.addr(Adresse), .data(Op0_data));
  ROM #(.addrWidth(10)) Op1 (.addr(Adresse), .data(Op1_data));
  ROM #(.addrWidth(10)) Result (.addr(Adresse), .data(Result_data));
  ALU alu_1 (
    .Flag_In(Flags_In_data), .Op0(Op0_data), .Op1(Op1_data), .Result(alu_1_result), .Flag_Out(alu_1_flag_out));  // open: CMD_15_12
  Comparator comparator_1 (.a(alu_1_result), .b(Result_data), .eq(comparator_1_eq));  // open: gt, lt
  ROM #(.addrWidth(10)) Flags_In (.addr(Adresse), .data(Flags_In_data));
  ROM #(.addrWidth(10)) Flag_result (.addr(Adresse), .data(Flag_result_data));
  Comparator comparator_2 (.a(Flag_result_data), .b(alu_1_flag_out), .eq(comparator_2_eq));  // open: gt, lt
  LED led_1 (.in(and_2_out));
  and and_2 (and_2_out, comparator_2_eq, comparator_1_eq);

  // Notes on the sheet:
  //   contents of Op0 (hex, n*v repeats v):
  //   1 2 3 aa ff
  //   contents of Op1 (hex, n*v repeats v):
  //   4 5 6 57 1
  //   contents of Result (hex, n*v repeats v):
  //   5 7 9 1
  //   CMD15_12
  //   Op1
  //   Result
  //   Op0
  //   Flag_In
  //   Flag_Out
  //   contents of Flag_result (hex, n*v repeats v):
  //   0 0 0 2 3
endmodule

module ShiftL (
  input  [7:0] Op,
  input  [7:0] Dist,
  input  CIn,
  output [7:0] Result,
  output COut
);

  wire comparator_1_eq;
  wire [3:0] subtractor_1_out;
  wire [8:0] shifter_1_out;

  Shifter #(.width(9)) shifter_1 (.in({Op, CIn}), .\dist (subtractor_1_out), .out(shifter_1_out));
  Subtractor #(.width(4)) subtractor_1 (.a(Dist[3:0]), .b(4'b0001), .out(subtractor_1_out));  // open: bin, bout
  Comparator comparator_1 (.a(Dist), .b({8{1'b0}}), .eq(comparator_1_eq));  // open: gt, lt
  Multiplexer #(.width(9)) multiplexer_1 (
    .in0(shifter_1_out), .in1({1'b0, Op}), .out({COut, Result}), .sel(comparator_1_eq));
endmodule
